# Fritzing sketch Fritzing (saved by Fritzing 0.9.1b)
breadboards: 2

parts:
  Part1 = Arduino Uno (Rev3)
  Part2 = Arduino Uno (Rev3)
  LCD1 = LCD screen
  LED1 = LED - 5mm [color="Red (633nm)" part_number=HeadLight2 package="5 mm [THT]"]
  LED2 = LED - 5mm [color="Red (633nm)" part_number=HeadLight1 package="5 mm [THT]"]
  LED3 = LED - 5mm [color="Red (633nm)" part_number=LeftBlinker package="5 mm [THT]"]
  LED4 = LED - 5mm [color="Red (633nm)" part_number=RightBlinker package="5 mm [THT]"]
  LED5 = LED - 5mm [color="Red (633nm)" part_number=BrakeLight package="5 mm [THT]"]
  LED6 = LED - 5mm [color="Red (633nm)" part_number=BrakeLight package="5 mm [THT]"]
  Part3 = Arduino Motor Shield (Rev3)
  R1 = Rotary Potentiometer (Large) [maximum_resistance=100kΩ package=THT]
  R2 = Resistor [tolerance=±5% resistance=330 package=THT]
  VCC1 = Battery
  VCC2 = Battery
  BAT1 = Battery Holders [package=battery-aa]
  IR1 = TSOP312.., 314.. [package=THT]
  R3 = Array Chip Resistor [part_number="330 Ohm Resistor Array" package=0603-arv]
  U1 = SPM0204UD5 [package=spm0204ud5]
  U2 = TEMPERATURE-SENSOR [package=to-92]

nets:
  N1: Part1.A0, Part3.A0, U2.ADJ
  N2: Part1.A1, Part3.A1
  N3: Part1.A2, Part3.A2
  N4: Part1.A3, Part3.A3
  N5: Part1.A5/SCL, Part2.A5/SCL, Part3.A5
  N6: Part1.D8, LED1.anode, LED2.anode, Part3.D8/BreakeB
  N7: Part1.D9_PWM, LED5.anode, LED6.anode, Part3.D9/BreakeA
  N8: Part1.D10_PWM/SS, LED3.anode, Part3.D10_PWM
  N9: Part1.D11_PWM/MOSI, LED4.anode, Part3.D11_PWM/B
  N10: Part1.D13/SCK, Part3.D13/DirB
  GND: Part1.GND, Part2.GND, LCD1.VSS, Part3.GND, R1.leg2, VCC1.-, IR1.GND, R3.A_1, R3.B_1, R3.C_1, R3.D_1, U1.GND#, U2.GND
  N11: Part1.AREF, Part3.AREF
  N12: Part1.D0/RX, Part3.IOREF#118
  N13: Part1.D1/TX, Part3.D1/TX
  N14: Part1.D2, Part3.D2, U1.GND
  N15: Part1.D3_PWM, Part3.D3_PWM/A, U1.OUT
  N16: Part1.D4, Part3.D4
  N17: Part1.D5_PWM, Part3.D5_PWM
  N18: Part1.D6_PWM, Part3.D6_PWM
  N19: Part1.D7, Part3.D7
  N20: Part1.ioref, Part3.IOREF#147
  N21: Part1.RESET, Part3.RESET
  3V3: Part1.3V3, Part3.3V3
  VIN: Part1.VIN, Part3.VMOT, Part3.VIN, VCC2.+
  N22: Part2.A4/SDA, Part3.A4
  N23: Part2.D2, LCD1.E
  N24: Part2.D3_PWM, LCD1.DB4
  N25: Part2.D4, LCD1.DB5
  N26: Part2.D5_PWM, LCD1.DB6
  N27: Part2.D6_PWM, LCD1.DB7
  N28: Part2.D7, LCD1.RS
  5V: Part2.5V, LCD1.VDD, LCD1.V0, R1.leg1, R1.wiper, R2.Pin_1
  VIN_2: Part2.VIN, Part3.5V, IR1.Vs, U1.VS, U2.VCC
  N29: LCD1.R/W, LCD1.LED-
  N30: LCD1.LED+, R2.Pin_0
  N31: LED1.cathode, LED2.cathode, R3.A_2
  N32: LED3.cathode, R3.C_2
  N33: LED4.cathode, R3.D_2
  N34: LED5.cathode, LED6.cathode, R3.B_2
  N35: Part3.D12/DirA, IR1.Data
  N36: VCC1.+, BAT1.+
  N37: VCC2.-, BAT1.-
